# Fritzing sketch BrewPiLess_Circuit (saved by Fritzing 0.9.4)
circuit board: 9.71676cm x 8.8367cm
breadboards: 7

parts:
  Li-Ion_Battery = 18650 battery holder [part_number="18650 3.7V" package=battery-18650-kit]
  C1 = Ceramic Capacitor [capacitance=1µF package="100 mil [THT, multilayer]"]
  C2 = Ceramic Capacitor [capacitance=1µF package="100 mil [THT, multilayer]"]
  Input = Screw terminal - 2 pins [part_number="DC 12V 1A" package=THT]
  Batery_Charger_Board = TP4056 [chip_label=TP4056 part_number=TP4056 package="DIP (Dual Inline) [THT]"]
  D1 = Diode [part_number=1N4001 package=diode-1n4001]
  Fuse = FUSE [part_number=1A package=fuse_5mm]
  R5 = Resistor [tolerance=±5% resistance=82 package=THT]
  R2 = Resistor [tolerance=±5% resistance=4.7k package=THT]
  Reset_Push_Button = Screw terminal - 2 pins [part_number=ESP-32 package=THT]
  NodeMCU_v1_0 = DOIT Esp32 DevKit v1 (30 pins long, 11 pins width) [part_number="ESP-32 30-Pin"]
  R4 = Resistor [tolerance=±5% resistance=82 package=THT]
  Chamber_Cooler_SSR_5V = screw terminal, 3 pins [part_number="GPIO 27"]
  R1 = Resistor [tolerance=±5% resistance=2.2k package=THT]
  Chamber_Heater_SSR_5V = screw terminal, 3 pins [part_number="GPIO 26"]
  Chamber_Cooler = LED - 3mm [color="Blue (470nm)" part_number="Blue 3mm" package="3 mm [THT]"]
  Chamber_Heater = LED - 3mm [color="Red (633nm)" part_number="Red 3mm" package="3 mm [THT]"]
  Humidity/Temp_Sensor_DHT22 = screw terminal, 3 pins [part_number="GPIO 19"]
  3_3V_Voltage_Regulator_250mA = MPC1700 [part_number="Low Quiescent Current (LDO)" package=sot23-3]
  Active_Buzzer_3V = Piezo Buzzer
  R3 = Resistor [tolerance=±5% resistance=10 package=THT]
  Temp_Sensors_DS18B20 = screw terminal, 3 pins [part_number="GPIO 23"]
  I2C = screw terminal, 4 pins [part_number="GPIO 21 and 22"]
  Chamber_Door_Switch = Screw terminal - 2 pins [part_number="GPIO 34" package=THT]
  Chamber_Light = LED - 3mm [color="Yellow (592nm)" part_number="Yellow 3mm" package="3 mm [THT]"]
  R6 = Resistor [tolerance=±5% resistance=82 package=THT]
  Chamber_Fan = LED - 3mm [color="Green (565nm)" part_number="Green 3mm" package="3 mm [THT]"]
  5V_Power_Regulator_Board = LM2596 step down module [part_number=LM2596]
  R8 = Resistor [tolerance=±5% resistance=1k package="0402 [SMD]"]
  Chamber_Light_2 = Screw terminal - 2 pins [part_number=12V package=THT]
  Q2 = NPN-Transistor [part_number="2N 2222" package="SOT-23 [SMD]"]
  R9 = Resistor [tolerance=±5% resistance=1k package="0402 [SMD]"]
  Q3 = NPN-Transistor [part_number="2N 2222" package="SOT-23 [SMD]"]
  Chamber_Circulation_Fans = Screw terminal - 2 pins [part_number=12V package=THT]
  R10 = Resistor [tolerance=±5% resistance=1k package="0402 [SMD]"]
  D3 = Diode [part_number=1N4148 package=diode-1n4148]
  D4 = Diode [part_number=1N4148 package=diode-1n4148]
  Chamber_Coller/Heater_Fan = Screw terminal - 2 pins [part_number=12V package=THT]
  Q1 = NPN-Transistor [part_number="2N 2222" package="SOT-23 [SMD]"]
  D2 = Diode [part_number=1N4148 package=diode-1n4148]
  R7 = Resistor [tolerance=±5% resistance=82 package=THT]
  Logic_Level_Converter = Logic Level Converter [part_number="4-Ch Bidirectional Module" package="Breakout board"]
  Multi_Wire_Cable_(Control) = screw terminal, 10 pins
  Multi_Wire_Cable_(Commands) = screw terminal, 5 pins

nets:
  N1: Li-Ion_Battery.+, Batery_Charger_Board.pin4
  N2: Li-Ion_Battery.-, Batery_Charger_Board.pin5
  GND: C1.0, C2.1, Input.pin1, Batery_Charger_Board.pin2, Batery_Charger_Board.pin6, D1.A, Reset_Push_Button.pin1, NodeMCU_v1_0.GND, Chamber_Cooler_SSR_5V.pin1, Chamber_Heater_SSR_5V.pin1, Chamber_Cooler.cathode, Chamber_Heater.cathode, Humidity/Temp_Sensor_DHT22.pin3, 3_3V_Voltage_Regulator_250mA.GND, Active_Buzzer_3V.pin_1, Temp_Sensors_DS18B20.pin3, I2C.pin4, Chamber_Light.cathode, Chamber_Fan.cathode, 5V_Power_Regulator_Board.IN-, 5V_Power_Regulator_Board.OUT-, Q2.2, Q3.2, Q1.2, Logic_Level_Converter.L-GND, Logic_Level_Converter.H-GND
  N3: C1.1, Batery_Charger_Board.pin3, 3_3V_Voltage_Regulator_250mA.IN
  3.3V: C2.0, R2.Pin_1, NodeMCU_v1_0.3V3, R1.Pin_1, Humidity/Temp_Sensor_DHT22.pin2, 3_3V_Voltage_Regulator_250mA.OUT, Temp_Sensors_DS18B20.pin2, I2C.pin3, Chamber_Door_Switch.pin1, Logic_Level_Converter.LV
  N4: Input.pin2, Fuse.2
  5V: Batery_Charger_Board.pin1, Chamber_Cooler_SSR_5V.pin2, Chamber_Heater_SSR_5V.pin2, 5V_Power_Regulator_Board.OUT+, Logic_Level_Converter.HV
  12V: D1.C, Fuse.1, 5V_Power_Regulator_Board.IN+, Chamber_Light_2.pin1, Chamber_Circulation_Fans.pin1, D3.C, D4.C, Chamber_Coller/Heater_Fan.pin1, D2.C
  N5: R5.Pin_0, Chamber_Heater.anode
  GPIO 26 Chamber Heater: R5.Pin_1, NodeMCU_v1_0.D26, Logic_Level_Converter.LV1
  GPIO 19 Humidity/Temp Sensor DHT22: R2.Pin_0, NodeMCU_v1_0.D19, Humidity/Temp_Sensor_DHT22.pin1
  µC Reset Push Button: Reset_Push_Button.pin2, NodeMCU_v1_0.EN
  GPIO 02 Chamber Light: NodeMCU_v1_0.D2, R6.Pin_1, R8.Pin_0
  GPIO 04 Buzzer: NodeMCU_v1_0.D4, R3.Pin_1
  GPIO 16 Circulation Fans: NodeMCU_v1_0.RX2, R10.Pin_0
  GPIO 17 FREE for Actuator: NodeMCU_v1_0.TX2
  GPIO 18 FREE for Actuator: NodeMCU_v1_0.D18
  GPIO 21 I2C (SDA): NodeMCU_v1_0.D21, I2C.pin1
  GPIO 22 I2C (SCL): NodeMCU_v1_0.D22, I2C.pin2
  GPIO 23 OneWire DS18B20: NodeMCU_v1_0.D23, R1.Pin_0, Temp_Sensors_DS18B20.pin1
  GPIO 34 Chamber Door Switch: NodeMCU_v1_0.D34, Chamber_Door_Switch.pin2
  GPIO 32 Rotatory A: NodeMCU_v1_0.D32
  GPIO 33 Rotatory B: NodeMCU_v1_0.D33
  GPIO 25 Rotatory Push: NodeMCU_v1_0.D25
  GPIO 27 Chamber Cooler: NodeMCU_v1_0.D27, R4.Pin_1, Logic_Level_Converter.LV2
  GPIO 14 Chamber Fan: NodeMCU_v1_0.D14, R9.Pin_0, R7.Pin_1
  N6: R4.Pin_0, Chamber_Cooler.anode
  N7: Chamber_Cooler_SSR_5V.pin3, Logic_Level_Converter.HV1
  N8: Chamber_Heater_SSR_5V.pin3, Logic_Level_Converter.HV2
  N9: Active_Buzzer_3V.pin_2, R3.Pin_0
  N10: Chamber_Light.anode, R6.Pin_0
  N11: Chamber_Fan.anode, R7.Pin_0
  N12: R8.Pin_1, Q1.0
  N13: Chamber_Light_2.pin2, Q1.1, D2.A
  N14: Q2.0, R9.Pin_1
  N15: Q2.1, D3.A, Chamber_Coller/Heater_Fan.pin2
  N16: Q3.0, R10.Pin_1
  N17: Q3.1, Chamber_Circulation_Fans.pin2, D4.A
  Black (GND): Multi_Wire_Cable_(Control).pin1, Multi_Wire_Cable_(Commands).pin1
  Violet (12V): Multi_Wire_Cable_(Control).pin2
  Red/White (5V): Multi_Wire_Cable_(Control).pin3
  Red (3,3V): Multi_Wire_Cable_(Control).pin4
  Blue/White (DHT): Multi_Wire_Cable_(Control).pin5
  White (Reset): Multi_Wire_Cable_(Control).pin6
  Yellow/White (OneWire): Multi_Wire_Cable_(Control).pin7
  Blue (Heater/Cooler Fan): Multi_Wire_Cable_(Control).pin8
  Green/White (Circulation Fans): Multi_Wire_Cable_(Control).pin9
  Gray (Light): Multi_Wire_Cable_(Control).pin10
  White (12V): Multi_Wire_Cable_(Commands).pin2
  Brown (5V): Multi_Wire_Cable_(Commands).pin3
  Blue (Cooler): Multi_Wire_Cable_(Commands).pin4
  Green (Heater): Multi_Wire_Cable_(Commands).pin5

notes:
  BrewPiLess Electronic Circuit, Electronic Circuit with UPS for BrewPiLess                        Author: Alcides Cremonezi (acremonezi@gmail.com), 4
  Power Supply
  Actuators
  Sensors and Display
  Microcontroller with BrewPiLess
  Buzzer and LEDs
  Light and Fans 12V Output
  Switches

custom parts:
  18650 battery holder: 18650 Battery Holder
  TP4056: A DIP stand-in part for whatever IC you want. With 6 pins on a 300mil dual inline package (DIP) footprint.
  DOIT Esp32 DevKit v1 (30 pins long, 11 pins width): The DOIT Esp32 DevKit v1 is one of the development board created by DOIT to evaluate the ESP-WROOM-32 module. It is based on the ESP32 microcontroller that boasts Wifi, Bluetooth, Ethernet and Low Power support all in a single chip. (vanepp) made breadboard work, adjusted pin numbering and labels and reduced size of schematic and cleaned up pcb. This chip is 30pins long (2 x15) and 11 pins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
  MPC1700: Small package LDO
  Piezo Buzzer: Part from https://www.nutsvolts.com/magazine/article/november2012_SmileysWorkshop modified to be .3 in spacing to match the adafruit buzzer 5V breadboard friendly part.
  LM2596 step down module: LM2596 DC-DC step down power supply module 3 A.
  Logic Level Converter: 5V to/from 3.3V logic level converter
